// Logisim project Carry Lookahead Adder.circ as structural Verilog: 4 circuits, main circuit CLA Generator
module CLA (
  input  A3,
  input  B3,
  input  A2,
  input  B2,
  input  A1,
  input  B1,
  input  A0,
  input  B0,
  input  Cin,
  output Cout,
  output S3,
  output S2,
  output S1,
  output S0
);

  wire cla_generator_1_c1, cla_generator_1_c2, cla_generator_1_c3, full_adder_1_generate,
       full_adder_1_propagate, full_adder_2_generate, full_adder_2_propagate, full_adder_3_generate,
       full_adder_3_propagate, full_adder_4_generate, full_adder_4_propagate, n7_segment_display_1_a_2,
       n7_segment_display_1_b_2, n7_segment_display_1_c_2, n7_segment_display_1_d_2, n7_segment_display_1_e,
       n7_segment_display_1_f, n7_segment_display_1_g, n7_segment_display_3_a_2, n7_segment_display_3_b_2,
       n7_segment_display_3_c_2, n7_segment_display_3_d_2, n7_segment_display_3_e, n7_segment_display_3_f,
       n7_segment_display_3_g, n7_segment_display_5_a_2, n7_segment_display_5_b_2, n7_segment_display_5_c_2,
       n7_segment_display_5_d_2, n7_segment_display_5_e, n7_segment_display_5_f, n7_segment_display_5_g;

  Full_Adder full_adder_1 (
    .A(A3), .B(B3), .C(cla_generator_1_c3), .Sum(S3), .Propagate(full_adder_1_propagate),
    .Generate(full_adder_1_generate));
  CLA_Generator cla_generator_1 (
    .c0(Cin), .C2(cla_generator_1_c2), .C4(Cout), .C3(cla_generator_1_c3), .C1(cla_generator_1_c1),
    .g0(full_adder_4_generate), .g1(full_adder_3_generate), .p1(full_adder_3_propagate),
    .g2(full_adder_2_generate), .g3(full_adder_1_generate), .p0(full_adder_4_propagate),
    .p2(full_adder_2_propagate), .p3(full_adder_1_propagate));
  Full_Adder full_adder_2 (
    .A(A2), .B(B2), .C(cla_generator_1_c2), .Sum(S2), .Propagate(full_adder_2_propagate),
    .Generate(full_adder_2_generate));
  Full_Adder full_adder_3 (
    .A(A1), .B(B1), .C(cla_generator_1_c1), .Sum(S1), .Propagate(full_adder_3_propagate),
    .Generate(full_adder_3_generate));
  Full_Adder full_adder_4 (
    .A(A0), .B(B0), .C(Cin), .Sum(S0), .Propagate(full_adder_4_propagate), .Generate(full_adder_4_generate));
  _7_Segment_Display u_7_segment_display_1 (
    .D(A3), .C(A2), .B(A1), .A(A0), .a_2(n7_segment_display_1_a_2), .b_2(n7_segment_display_1_b_2),
    .c_2(n7_segment_display_1_c_2), .d_2(n7_segment_display_1_d_2), .e(n7_segment_display_1_e),
    .f(n7_segment_display_1_f), .g(n7_segment_display_1_g));
  _7_Segment_Display_part u_7_segment_display_2 (
    .g(n7_segment_display_1_g), .f(n7_segment_display_1_f), .a(n7_segment_display_1_a_2),
    .b(n7_segment_display_1_b_2), .e(n7_segment_display_1_e), .d(n7_segment_display_1_d_2),
    .c(n7_segment_display_1_c_2));  // open: dp
  _7_Segment_Display u_7_segment_display_3 (
    .D(B3), .C(B2), .B(B1), .A(B0), .a_2(n7_segment_display_3_a_2), .b_2(n7_segment_display_3_b_2),
    .c_2(n7_segment_display_3_c_2), .d_2(n7_segment_display_3_d_2), .e(n7_segment_display_3_e),
    .f(n7_segment_display_3_f), .g(n7_segment_display_3_g));
  _7_Segment_Display_part u_7_segment_display_4 (
    .g(n7_segment_display_3_g), .f(n7_segment_display_3_f), .a(n7_segment_display_3_a_2),
    .b(n7_segment_display_3_b_2), .e(n7_segment_display_3_e), .d(n7_segment_display_3_d_2),
    .c(n7_segment_display_3_c_2));  // open: dp
  _7_Segment_Display u_7_segment_display_5 (
    .D(S3), .C(S2), .B(S1), .A(S0), .a_2(n7_segment_display_5_a_2), .b_2(n7_segment_display_5_b_2),
    .c_2(n7_segment_display_5_c_2), .d_2(n7_segment_display_5_d_2), .e(n7_segment_display_5_e),
    .f(n7_segment_display_5_f), .g(n7_segment_display_5_g));
  _7_Segment_Display_part u_7_segment_display_6 (
    .g(n7_segment_display_5_g), .f(n7_segment_display_5_f), .a(n7_segment_display_5_a_2),
    .b(n7_segment_display_5_b_2), .e(n7_segment_display_5_e), .d(n7_segment_display_5_d_2),
    .c(n7_segment_display_5_c_2));  // open: dp

  // Notes on the sheet:
  //   Carry Lookahead Adder
endmodule

// CLA Logic
module CLA_Generator (
  input  c0,
  input  g0,
  input  g1,
  input  g2,
  input  g3,
  input  p0,
  input  p1,
  input  p2,
  input  p3,
  output C1,
  output C2,
  output C3,
  output C4
);

  wire and_1_out, and_2_out, and_3_out, and_4_out, and_5_out, and_6_out, and_7_out, and_8_out, and_9_out,
       and_10_out;

  and and_1 (and_1_out, c0, p3, p2, p1, p0);
  and and_2 (and_2_out, g3, p2, p1, p0);
  and and_3 (and_3_out, g2, p1, p0);
  and and_4 (and_4_out, g1, p0);
  and and_5 (and_5_out, c0, p3, p2, p1);
  and and_6 (and_6_out, g3, p2, p1);
  and and_7 (and_7_out, g2, p1);
  and and_8 (and_8_out, c0, p2, p3);
  and and_9 (and_9_out, p2, g3);
  and and_10 (and_10_out, c0, p3);
  or or_1 (C1, and_1_out, and_2_out, and_3_out, and_4_out, g0);
  or or_2 (C2, and_5_out, and_6_out, and_7_out, g1);
  or or_3 (C3, and_8_out, and_9_out, g2);
  or or_4 (C4, and_10_out, g3);

  // Notes on the sheet:
  //   Carry Lookahead Logic
endmodule

// 1-bit FA
module Full_Adder (
  input  A,
  input  B,
  input  C,
  output Generate,
  output Propagate,
  output Sum
);

  wire xor_1_out;

  xor xor_1 (xor_1_out, A, B);
  and and_1 (Generate, A, B);
  or or_1 (Propagate, A, B);
  xor xor_2 (Sum, xor_1_out, C);

  // Notes on the sheet:
  //   Full Adder
endmodule

module _7_Segment_Display (
  input  D,
  input  C,
  input  B,
  input  A,
  output a_2,
  output b_2,
  output c_2,
  output d_2,
  output e,
  output f,
  output g
);

  wire nand_1_out, nand_2_out, nand_3_out, nand_4_out, nand_5_out, nand_6_out, nand_7_out, nand_8_out,
       nand_9_out, nand_10_out, nand_11_out, nand_12_out, nand_13_out, nand_14_out, nand_15_out, nand_16_out,
       nand_17_out, nand_18_out, nand_19_out, nand_20_out, nand_21_out, nand_22_out, nand_23_out,
       nand_24_out, nand_25_out, nand_26_out, nand_27_out, nand_28_out, nand_29_out, nand_30_out,
       nand_31_out, nand_32_out, nand_33_out, nand_34_out, nand_35_out, nand_36_out, nand_37_out,
       nand_38_out, nand_39_out, nand_40_out, nand_41_out, nand_42_out, nand_43_out, nand_44_out,
       nand_45_out, nand_46_out, nand_47_out, nand_48_out, nand_49_out, nand_50_out, nand_51_out,
       nand_52_out, nand_53_out, nand_54_out, nand_55_out, nand_56_out, nand_57_out, nand_58_out,
       nand_59_out, nand_60_out, nand_61_out, nand_62_out, nand_63_out, nand_64_out, nand_65_out,
       nand_66_out, nand_67_out, nand_68_out, nand_69_out, nand_70_out, nand_71_out, nand_72_out,
       nand_73_out, nand_74_out, nand_75_out, nand_76_out, nand_77_out, nand_78_out, nand_79_out,
       nand_80_out, nand_81_out, nand_82_out, nand_83_out, nand_84_out, nand_85_out, nand_86_out,
       nand_87_out, nand_88_out, nand_89_out, nand_90_out, nand_91_out, nand_92_out, nand_93_out,
       nand_94_out, nand_95_out, nand_96_out, nand_97_out, nand_98_out, nand_99_out, nand_100_out,
       nand_101_out, nand_102_out, nand_103_out, nand_104_out, nand_106_out, nand_107_out, nand_108_out,
       nand_109_out, nand_110_out, nand_111_out, nand_112_out, nand_113_out, nand_114_out, nand_115_out,
       nand_116_out, nand_117_out, nand_118_out, nand_119_out, nand_120_out, nand_121_out, nand_122_out,
       nand_123_out, nand_124_out, nand_125_out, nand_126_out, nand_127_out, nand_128_out, nand_129_out,
       nand_130_out, nand_131_out, nand_132_out, nand_133_out, nand_134_out, nand_136_out, nand_137_out,
       nand_138_out, nand_139_out, nand_141_out, nand_142_out, nand_143_out, nand_144_out, nand_145_out,
       nand_146_out, nand_147_out, nand_148_out;

  nand nand_1 (nand_1_out, C, C);
  nand nand_2 (nand_2_out, D, D);
  nand nand_3 (nand_3_out, B, B);
  nand nand_4 (nand_4_out, D, D);
  nand nand_5 (nand_5_out, B, B);
  nand nand_6 (nand_6_out, D, D);
  nand nand_7 (nand_7_out, D, D);
  nand nand_8 (nand_8_out, C, C);
  nand nand_9 (nand_9_out, C, C);
  nand nand_10 (nand_10_out, C, C);
  nand nand_11 (nand_11_out, A, A);
  nand nand_12 (nand_12_out, A, A);
  nand nand_13 (nand_13_out, D, D);
  nand nand_14 (nand_14_out, C, C);
  nand nand_15 (nand_15_out, A, A);
  nand nand_16 (nand_16_out, D, D);
  nand nand_17 (nand_17_out, D, nand_1_out);
  nand nand_18 (nand_18_out, nand_2_out, nand_3_out);
  nand nand_19 (nand_19_out, nand_4_out, nand_5_out);
  nand nand_20 (nand_20_out, nand_6_out, A);
  nand nand_21 (nand_21_out, nand_7_out, nand_8_out);
  nand nand_22 (nand_22_out, nand_9_out, B);
  nand nand_23 (nand_23_out, nand_10_out, nand_11_out);
  nand nand_24 (nand_24_out, B, nand_12_out);
  nand nand_25 (nand_25_out, D, B);
  nand nand_26 (nand_26_out, D, C);
  nand nand_27 (nand_27_out, nand_13_out, C);
  nand nand_28 (nand_28_out, nand_14_out, B);
  nand nand_29 (nand_29_out, B, nand_15_out);
  nand nand_30 (nand_30_out, nand_16_out, C);
  nand nand_31 (nand_31_out, C, C);
  nand nand_32 (nand_32_out, A, A);
  nand nand_33 (nand_33_out, D, D);
  nand nand_34 (nand_34_out, D, D);
  nand nand_35 (nand_35_out, nand_17_out, nand_17_out);
  nand nand_36 (nand_36_out, B, B);
  nand nand_37 (nand_37_out, D, D);
  nand nand_38 (nand_38_out, C, C);
  nand nand_39 (nand_39_out, nand_18_out, nand_18_out);
  nand nand_40 (nand_40_out, A, A);
  nand nand_41 (nand_41_out, D, D);
  nand nand_42 (nand_42_out, B, B);
  nand nand_43 (nand_43_out, nand_19_out, nand_20_out);
  nand nand_44 (nand_44_out, B, B);
  nand nand_45 (nand_45_out, D, D);
  nand nand_46 (nand_46_out, C, C);
  nand nand_47 (nand_47_out, nand_21_out, nand_21_out);
  nand nand_48 (nand_48_out, A, A);
  nand nand_49 (nand_49_out, nand_22_out, nand_22_out);
  nand nand_50 (nand_50_out, B, B);
  nand nand_51 (nand_51_out, B, B);
  nand nand_52 (nand_52_out, nand_23_out, nand_24_out);
  nand nand_53 (nand_53_out, nand_25_out, nand_26_out);
  nand nand_54 (nand_54_out, B, B);
  nand nand_55 (nand_55_out, A, A);
  nand nand_56 (nand_56_out, nand_27_out, nand_27_out);
  nand nand_57 (nand_57_out, B, B);
  nand nand_58 (nand_58_out, nand_28_out, nand_29_out);
  nand nand_59 (nand_59_out, nand_30_out, nand_30_out);
  nand nand_60 (nand_60_out, B, B);
  nand nand_61 (nand_61_out, C, C);
  nand nand_62 (nand_62_out, nand_31_out, nand_32_out);
  nand nand_63 (nand_63_out, nand_33_out, B);
  nand nand_64 (nand_64_out, nand_34_out, C);
  nand nand_65 (nand_65_out, C, B);
  nand nand_66 (nand_66_out, nand_35_out, nand_36_out);
  nand nand_67 (nand_67_out, nand_37_out, nand_38_out);
  nand nand_68 (nand_68_out, nand_39_out, nand_40_out);
  nand nand_69 (nand_69_out, nand_41_out, B);
  nand nand_70 (nand_70_out, D, nand_42_out);
  nand nand_71 (nand_71_out, nand_43_out, nand_43_out);
  nand nand_72 (nand_72_out, nand_44_out, A);
  nand nand_73 (nand_73_out, nand_45_out, C);
  nand nand_74 (nand_74_out, D, nand_46_out);
  nand nand_75 (nand_75_out, nand_47_out, nand_48_out);
  nand nand_76 (nand_76_out, nand_49_out, A);
  nand nand_77 (nand_77_out, C, nand_50_out);
  nand nand_78 (nand_78_out, C, B);
  nand nand_79 (nand_79_out, D, nand_51_out);
  nand nand_80 (nand_80_out, nand_52_out, nand_52_out);
  nand nand_81 (nand_81_out, nand_53_out, nand_53_out);
  nand nand_82 (nand_82_out, nand_54_out, nand_55_out);
  nand nand_83 (nand_83_out, nand_56_out, nand_57_out);
  nand nand_84 (nand_84_out, nand_58_out, nand_58_out);
  nand nand_85 (nand_85_out, nand_59_out, nand_60_out);
  nand nand_86 (nand_86_out, D, nand_61_out);
  nand nand_87 (nand_87_out, D, A);
  nand nand_88 (nand_88_out, nand_62_out, nand_63_out);
  nand nand_89 (nand_89_out, nand_64_out, nand_64_out);
  nand nand_90 (nand_90_out, nand_65_out, nand_66_out);
  nand nand_91 (nand_91_out, A, A);
  nand nand_92 (nand_92_out, nand_67_out, nand_68_out);
  nand nand_93 (nand_93_out, C, C);
  nand nand_94 (nand_94_out, A, A);
  nand nand_95 (nand_95_out, nand_69_out, nand_69_out);
  nand nand_96 (nand_96_out, nand_70_out, nand_70_out);
  nand nand_97 (nand_97_out, nand_71_out, nand_72_out);
  nand nand_98 (nand_98_out, nand_73_out, nand_74_out);
  nand nand_99 (nand_99_out, nand_75_out, nand_76_out);
  nand nand_100 (nand_100_out, nand_77_out, nand_77_out);
  nand nand_101 (nand_101_out, nand_78_out, nand_78_out);
  nand nand_102 (nand_102_out, A, A);
  nand nand_103 (nand_103_out, nand_79_out, nand_79_out);
  nand nand_104 (nand_104_out, A, A);
  nand nand_105 (e, nand_80_out, nand_81_out);
  nand nand_106 (nand_106_out, nand_82_out, nand_83_out);
  nand nand_107 (nand_107_out, A, A);
  nand nand_108 (nand_108_out, C, C);
  nand nand_109 (nand_109_out, nand_84_out, nand_85_out);
  nand nand_110 (nand_110_out, nand_86_out, nand_87_out);
  nand nand_111 (nand_111_out, nand_88_out, nand_88_out);
  nand nand_112 (nand_112_out, nand_89_out, A);
  nand nand_113 (nand_113_out, nand_90_out, nand_90_out);
  nand nand_114 (nand_114_out, D, nand_91_out);
  nand nand_115 (nand_115_out, nand_92_out, nand_92_out);
  nand nand_116 (nand_116_out, nand_93_out, nand_94_out);
  nand nand_117 (nand_117_out, nand_95_out, A);
  nand nand_118 (nand_118_out, nand_96_out, A);
  nand nand_119 (nand_119_out, nand_97_out, nand_97_out);
  nand nand_120 (nand_120_out, nand_98_out, nand_98_out);
  nand nand_121 (nand_121_out, nand_99_out, nand_99_out);
  nand nand_122 (nand_122_out, nand_100_out, A);
  nand nand_123 (nand_123_out, nand_101_out, nand_102_out);
  nand nand_124 (nand_124_out, nand_103_out, nand_104_out);
  nand nand_125 (nand_125_out, nand_106_out, nand_106_out);
  nand nand_126 (nand_126_out, C, nand_107_out);
  nand nand_127 (nand_127_out, D, nand_108_out);
  nand nand_128 (nand_128_out, D, B);
  nand nand_129 (nand_129_out, nand_109_out, nand_109_out);
  nand nand_130 (nand_130_out, nand_110_out, nand_110_out);
  nand nand_131 (nand_131_out, nand_111_out, nand_112_out);
  nand nand_132 (nand_132_out, nand_113_out, nand_114_out);
  nand nand_133 (nand_133_out, nand_115_out, nand_116_out);
  nand nand_134 (nand_134_out, nand_117_out, nand_118_out);
  nand nand_135 (c_2, nand_119_out, nand_120_out);
  nand nand_136 (nand_136_out, nand_121_out, nand_122_out);
  nand nand_137 (nand_137_out, nand_123_out, nand_124_out);
  nand nand_138 (nand_138_out, nand_125_out, nand_126_out);
  nand nand_139 (nand_139_out, nand_127_out, nand_128_out);
  nand nand_140 (g, nand_129_out, nand_130_out);
  nand nand_141 (nand_141_out, nand_131_out, nand_131_out);
  nand nand_142 (nand_142_out, nand_132_out, nand_132_out);
  nand nand_143 (nand_143_out, nand_133_out, nand_133_out);
  nand nand_144 (nand_144_out, nand_134_out, nand_134_out);
  nand nand_145 (nand_145_out, nand_136_out, nand_136_out);
  nand nand_146 (nand_146_out, nand_137_out, nand_137_out);
  nand nand_147 (nand_147_out, nand_138_out, nand_138_out);
  nand nand_148 (nand_148_out, nand_139_out, nand_139_out);
  nand nand_149 (a_2, nand_141_out, nand_142_out);
  nand nand_150 (b_2, nand_143_out, nand_144_out);
  nand nand_151 (d_2, nand_145_out, nand_146_out);
  nand nand_152 (f, nand_147_out, nand_148_out);

  // Notes on the sheet:
  //   7 Segment Display
  //   NAND-NAND implementation courtesy of http://github.com/marceloboeira
endmodule
